// Logisim project cdm-platform.circ as structural Verilog: 1 circuit, main circuit Main
module Main (
);

  wire button_1_out, button_2_out, button_3_out, button_4_out, button_5_out, button_6_out, button_7_out,
       button_8_out, button_9_out, button_10_out, button_11_out, button_12_out, cdm_8_mark5_1_data_inst,
       Clock, Data, I_O, IAck, Inst, io_double_hex_1_dot_1, io_double_hex_1_dot_2, io_seven_segment_1_a,
       io_seven_segment_1_b, io_seven_segment_1_c, io_seven_segment_1_d, io_seven_segment_1_dot,
       io_seven_segment_1_e, io_seven_segment_1_f, io_seven_segment_1_g, io_seven_segment_2_a,
       io_seven_segment_2_b, io_seven_segment_2_c, io_seven_segment_2_d, io_seven_segment_2_dot,
       io_seven_segment_2_e, io_seven_segment_2_f, io_seven_segment_2_g, IR_Enable,
       ir_enable_buffer_1_int0_2, ir_enable_buffer_1_int1_2, ir_enable_buffer_1_int2_2,
       ir_enable_buffer_1_int3_2, ir_enable_buffer_1_int4_2, ir_enable_buffer_1_int5_2,
       ir_enable_buffer_1_int6_2, ir_enable_buffer_1_int7_2, irarb_1_ia0, irarb_1_ia1, irarb_1_ia2,
       irarb_1_ia3, irarb_1_ia4, irarb_1_ia5, irarb_1_ia6, irarb_1_ia7, IRQ, keyboard_1_avail, mem,
       not_1_out, RAM_Global, RAM_Paged, rd_wr_prime, ROM, terminal_controller_1_keyboard_clock,
       terminal_controller_1_keyboard_enable, terminal_controller_1_terminal_clear,
       terminal_controller_1_terminal_clock, terminal_controller_1_terminal_enable, Vector;
  wire [2:0] vec;
  wire [3:0] I_O_Address, io_double_hex_1_data_hi_out, io_double_hex_1_data_low_out;
  wire [6:0] keyboard_1_data, RAM_Global_Address, terminal_controller_1_terminal_data;
  wire [7:0] Address_Bus, cdm_8_mark5_1_data_out, controlled_buffer_1_out, Data_Bus, io_reg_1_data_out, PC,
       PS, R0, R1, R2, R3, ROM_Address_Hi, SP;
  wire [11:0] RAM_Paged_Address;
  wire [31:0] display_controller_color_1_colomn_scan_b, display_controller_color_1_colomn_scan_g,
       display_controller_color_1_colomn_scan_r, display_controller_color_1_data_blue,
       display_controller_color_1_data_green, display_controller_color_1_data_red,
       display_controller_color_2_colomn_scan_b, display_controller_color_2_colomn_scan_g,
       display_controller_color_2_colomn_scan_r, display_controller_color_2_data_blue,
       display_controller_color_2_data_green, display_controller_color_2_data_red;

  TTY tty_1 (
    .data(terminal_controller_1_terminal_data), .clk(terminal_controller_1_terminal_clock),
    .we(terminal_controller_1_terminal_enable), .clr(terminal_controller_1_terminal_clear));
  // Probe on R0
  // Probe on R0
  // Probe on R0
  // Probe on R1
  // Probe on R1
  // Probe on R1
  // Probe on R2
  // Probe on R2
  // Probe on R2
  // Probe on R3
  // Probe on R3
  // Probe on R3
  Button button_1 (.out(button_1_out));
  Button button_2 (.out(button_2_out));
  Button button_3 (.out(button_3_out));
  Keyboard keyboard_1 (
    .clk(terminal_controller_1_keyboard_clock), .re(terminal_controller_1_keyboard_enable),
    .avail(keyboard_1_avail), .data(keyboard_1_data));  // open: clr
  Terminal_Controller terminal_controller_1 (
    .Keyboard_Enable(terminal_controller_1_keyboard_enable),
    .Keyboard_Clock(terminal_controller_1_keyboard_clock), .Keyboard_Data(keyboard_1_data),
    .Keyboard_Available(keyboard_1_avail), .Terminal_Data(terminal_controller_1_terminal_data),
    .Terminal_Clear(terminal_controller_1_terminal_clear),
    .Terminal_Clock(terminal_controller_1_terminal_clock),
    .Terminal_Enable(terminal_controller_1_terminal_enable));  // open: Clock, rd_wr_prime, IO_Address, IO, Device_Address, IRQ, Data_Bus_In, Data_Bus_Out
  // Probe on R0
  // Probe on PC
  // Probe on R1
  // Probe on SP
  // Probe on R2
  // Probe on R3
  Clock clock_1 (.out(Clock));
  IrArb irarb_1 (
    .IAck(IAck), .Vector(vec), .IRQ(IRQ), .INT0(ir_enable_buffer_1_int0_2), .IA0(irarb_1_ia0),
    .INT1(ir_enable_buffer_1_int1_2), .IA1(irarb_1_ia1), .INT2(ir_enable_buffer_1_int2_2), .IA2(irarb_1_ia2),
    .INT3(ir_enable_buffer_1_int3_2), .IA3(irarb_1_ia3), .INT4(ir_enable_buffer_1_int4_2), .IA4(irarb_1_ia4),
    .INT5(ir_enable_buffer_1_int5_2), .IA5(irarb_1_ia5), .INT6(ir_enable_buffer_1_int6_2), .IA6(irarb_1_ia6),
    .INT7(ir_enable_buffer_1_int7_2), .IA7(irarb_1_ia7));
  Ir_Enable_Buffer ir_enable_buffer_1 (
    .Data_Bus_In(Data_Bus), .rd_wr_prime(rd_wr_prime), .IO_Address(I_O_Address), .IO(I_O),
    .Device_Address(4'b0000), .Clock(Clock), .Data_Bus_Out(Data_Bus), .INT0(button_2_out),
    .INT1(button_1_out), .INT2(button_3_out), .INT3(button_7_out), .INT4(button_4_out), .INT5(button_6_out),
    .INT6(button_5_out), .INT7(button_8_out), .INT0_2(ir_enable_buffer_1_int0_2), .IA0(irarb_1_ia0),
    .INT1_2(ir_enable_buffer_1_int1_2), .IA1(irarb_1_ia1), .INT2_2(ir_enable_buffer_1_int2_2),
    .IA2(irarb_1_ia2), .INT3_2(ir_enable_buffer_1_int3_2), .IA3(irarb_1_ia3),
    .INT4_2(ir_enable_buffer_1_int4_2), .IA4(irarb_1_ia4), .INT5_2(ir_enable_buffer_1_int5_2),
    .IA5(irarb_1_ia5), .INT6_2(ir_enable_buffer_1_int6_2), .IA6(irarb_1_ia6),
    .INT7_2(ir_enable_buffer_1_int7_2), .IA7(irarb_1_ia7), .Enable(IR_Enable));  // open: IA0_2, IA1_2, IA2_2, IA3_2, IA4_2, IA5_2, IA6_2, IA7_2
  Button button_4 (.out(button_4_out));
  Button button_5 (.out(button_5_out));
  Button button_6 (.out(button_6_out));
  Button button_7 (.out(button_7_out));
  // Probe on PC
  // Probe on PC
  // Probe on SP
  // Probe on SP
  // Probe on PS
  Button button_8 (.out(button_8_out));
  Button button_9 (.out(button_9_out));
  Button button_10 (.out(button_10_out));
  Button button_11 (.out(button_11_out));
  Button button_12 (.out(button_12_out));
  IO_Random_Number_Generator io_random_number_generator_1 (
    .Clock(Clock), .rd_wr_prime(rd_wr_prime), .IO_Address(I_O_Address), .IO(I_O), .Device_Address(4'b0001),
    .Data_Bus_Out(Data_Bus));
  CdM_8_mark5 cdm_8_mark5_1 (
    .clock(Clock), .addr(Address_Bus), .mem_read(rd_wr_prime), .mem_cycle(mem),
    .data_inst(cdm_8_mark5_1_data_inst), .data_out(cdm_8_mark5_1_data_out),
    .data_in(controlled_buffer_1_out), .r0(R0), .r1(R1), .r2(R2), .r3(R3), .PC(PC), .SP(SP), .PS(PS),
    .IAck(IAck), .IRQ(IRQ), .vec(vec));
  assign controlled_buffer_1_out = rd_wr_prime ? Data_Bus : 8'bz;  // Controlled_Buffer controlled_buffer_1
  Hex_Digit_Display hex_digit_display_1 (.value(io_double_hex_1_data_hi_out), .dp(io_double_hex_1_dot_1));
  IO_Double_Hex io_double_hex_1 (
    .Data_Low_Out(io_double_hex_1_data_low_out), .Data_Hi_Out(io_double_hex_1_data_hi_out),
    .Dot_1(io_double_hex_1_dot_1), .Dot_2(io_double_hex_1_dot_2));  // open: Data_Bus_In, rd_wr_prime, IO_Address, IO, Device_Address, Clock, Data_Bus_Out
  Address_Decoder address_decoder_1 (
    .data_ins_prime(cdm_8_mark5_1_data_inst), .memory(mem), .Address_Bus(Address_Bus), .Inst(Inst),
    .Data(Data), .Vector(Vector), .I_O(I_O), .ROM(ROM), .RAM_Global(RAM_Global), .RAM_Paged(RAM_Paged),
    .I_O_Address(I_O_Address));
  assign Data_Bus = not_1_out ? cdm_8_mark5_1_data_out : 8'bz;  // Controlled_Buffer controlled_buffer_2
  not not_1 (not_1_out, rd_wr_prime);
  Hex_Digit_Display hex_digit_display_2 (.value(io_double_hex_1_data_low_out), .dp(io_double_hex_1_dot_2));
  // Keypad_Controller keypad_controller_1: pin names not known
  Joystick joystick_1 ();  // open: x, y
  RAM_Controller ram_controller_1 (
    .Clock(Clock), .rd_wr_prime(rd_wr_prime), .IO_Address(I_O_Address), .IO(I_O), .Device_Address(4'b1110),
    .Data_Bus_In(Data_Bus), .Data_Bus_Out(Data_Bus), .Address_Bus(Address_Bus),
    .RAM_Global_Address(RAM_Global_Address), .RAM_Paged_Address(RAM_Paged_Address));
  Display_Controller_Color display_controller_color_1 (
    .Data_Bus_In(Data_Bus), .Data_Bus_Out(Data_Bus), .Clock(Clock), .rd_wr_prime(rd_wr_prime),
    .IO_Address(I_O_Address), .IO(I_O), .Device_Address(4'b1010), .Fast_Clock(Clock),
    .Data_Red(display_controller_color_1_data_red), .Data_Green(display_controller_color_1_data_green),
    .Colomn_Scan_R(display_controller_color_1_colomn_scan_r),
    .Data_Blue(display_controller_color_1_data_blue),
    .Colomn_Scan_G(display_controller_color_1_colomn_scan_g),
    .Colomn_Scan_B(display_controller_color_1_colomn_scan_b));
  // DotMatrix #(.inputtype("select"), .matrixcols(32), .matrixrows(32), .persist(64)) dotmatrix_1: pin names not known; wires that end beside it: display_controller_color_1_colomn_scan_g, display_controller_color_1_data_green
  // DotMatrix #(.inputtype("select"), .matrixcols(32), .matrixrows(32), .persist(64)) dotmatrix_2: pin names not known; wires that end beside it: display_controller_color_1_colomn_scan_r, display_controller_color_1_data_red
  // DotMatrix #(.inputtype("select"), .matrixcols(32), .matrixrows(32), .persist(64)) dotmatrix_3: pin names not known; wires that end beside it: display_controller_color_1_colomn_scan_b, display_controller_color_1_data_blue
  IO_Reg io_reg_1 (
    .Data_Bus_In(Data_Bus), .rd_wr_prime(rd_wr_prime), .IO_Address(I_O_Address), .IO(I_O),
    .Device_Address(4'b0010), .Clock(Clock), .Data_Bus_Out(Data_Bus), .Data_Out(io_reg_1_data_out));
  ROM_Controller rom_controller_1 (
    .Clock(Clock), .rd_wr_prime(rd_wr_prime), .IO_Address(I_O_Address), .IO(I_O), .Device_Address(4'b1000),
    .ISR_Bank(io_reg_1_data_out), .Data_Bus_In(Data_Bus), .Data_Bus_Out(Data_Bus),
    .Addrerss_Out(ROM_Address_Hi), .IAck(IAck), .IR_Enable(IR_Enable));
  RAM #(.addrWidth(7)) ram_1 (
    .addr(RAM_Global_Address), .data(Data_Bus), .sel(RAM_Global), .clk(Clock), .ld(rd_wr_prime));  // open: clr
  RAM #(.addrWidth(12)) ram_2 (
    .addr(RAM_Paged_Address), .data(Data_Bus), .sel(RAM_Paged), .clk(Clock), .ld(rd_wr_prime));  // open: clr
  _7_Segment_Display u_7_segment_display_1 (
    .g(io_seven_segment_2_g), .f(io_seven_segment_2_f), .a(io_seven_segment_2_a), .b(io_seven_segment_2_b),
    .e(io_seven_segment_2_e), .d(io_seven_segment_2_d), .c(io_seven_segment_2_c), .dp(io_seven_segment_2_dot));
  _7_Segment_Display u_7_segment_display_2 (
    .g(io_seven_segment_1_g), .f(io_seven_segment_1_f), .a(io_seven_segment_1_a), .b(io_seven_segment_1_b),
    .e(io_seven_segment_1_e), .d(io_seven_segment_1_d), .c(io_seven_segment_1_c), .dp(io_seven_segment_1_dot));
  IO_Seven_Segment io_seven_segment_1 (
    .A(io_seven_segment_1_a), .B(io_seven_segment_1_b), .C(io_seven_segment_1_c), .D(io_seven_segment_1_d),
    .E(io_seven_segment_1_e), .F(io_seven_segment_1_f), .G(io_seven_segment_1_g), .Dot(io_seven_segment_1_dot));  // open: Data_Bus_In, rd_wr_prime, IO_Address, IO, Device_Address, Clock, Data_Bus_Out
  IO_Seven_Segment io_seven_segment_2 (
    .A(io_seven_segment_2_a), .B(io_seven_segment_2_b), .C(io_seven_segment_2_c), .D(io_seven_segment_2_d),
    .E(io_seven_segment_2_e), .F(io_seven_segment_2_f), .G(io_seven_segment_2_g), .Dot(io_seven_segment_2_dot));  // open: Data_Bus_In, rd_wr_prime, IO_Address, IO, Device_Address, Clock, Data_Bus_Out
  Display_Controller_Color display_controller_color_2 (
    .Data_Bus_In(Data_Bus), .Data_Bus_Out(Data_Bus), .Clock(Clock), .rd_wr_prime(rd_wr_prime),
    .IO_Address(I_O_Address), .IO(I_O), .Device_Address(4'b1011), .Fast_Clock(Clock),
    .Data_Red(display_controller_color_2_data_red), .Data_Green(display_controller_color_2_data_green),
    .Colomn_Scan_R(display_controller_color_2_colomn_scan_r),
    .Data_Blue(display_controller_color_2_data_blue),
    .Colomn_Scan_G(display_controller_color_2_colomn_scan_g),
    .Colomn_Scan_B(display_controller_color_2_colomn_scan_b));
  // DotMatrix #(.inputtype("select"), .matrixcols(32), .matrixrows(32), .persist(64)) dotmatrix_4: pin names not known; wires that end beside it: display_controller_color_2_colomn_scan_b, display_controller_color_2_data_blue
  // DotMatrix #(.inputtype("select"), .matrixcols(32), .matrixrows(32), .persist(64)) dotmatrix_5: pin names not known; wires that end beside it: display_controller_color_2_colomn_scan_g, display_controller_color_2_data_green
  // DotMatrix #(.inputtype("select"), .matrixcols(32), .matrixrows(32), .persist(64)) dotmatrix_6: pin names not known; wires that end beside it: display_controller_color_2_colomn_scan_r, display_controller_color_2_data_red
  // RAM ram_3: pin names not known; wires that end beside it: {ROM_Address_Hi[3:0], Address_Bus}, ROM, Data_Bus
endmodule
